# Fritzing sketch single_reset_s (saved by Fritzing 1.0.1rc)
breadboards: 1

parts:
  WeMos_D1_Mini1 = WeMos D1 Mini
  S1 = Pushbutton [package="[THT]"]
  Q1_2N3904 = TRANSISTOR_NPN [package=to-92]
  R1 = Resistor [tolerance=±5% power=0.25 resistance=10k package=THT]
  C1_0_47_µF = Capacitor [package=cap-pth-small2]

nets:
  N1: WeMos_D1_Mini1.3V3, S1.Pin_3, S1.Pin_4
  N2: WeMos_D1_Mini1.D1, Q1_2N3904.C, C1_0_47_µF.2
  N3: WeMos_D1_Mini1.G, Q1_2N3904.E
  N4: WeMos_D1_Mini1.RST, C1_0_47_µF.1
  N5: S1.Pin_1, S1.Pin_2, R1.Pin_0
  N6: Q1_2N3904.B, R1.Pin_1
